// Logisim project port_dekoder.circ as structural Verilog: 1 circuit, main circuit main
module main (
  input  NRD,
  input  NDI_ULA,
  input  NWR,
  input  NIORQ,
  input  A1,
  input  A0,
  input  DI_32765,
  input  A5,
  input  A7,
  input  NM1,
  input  A14,
  input  A15,
  output NIN254,
  output NOUT254,
  output CS_32765,
  output BC1,
  output BDIR
);

  wire buffer_1_out, I1_out, I2_2_out, I2_out, I3_2_out, I3_out, I4_out, I5_out, I13_out, I14_out, I15_out,
       I16_out, nand_1_out, nand_2_out, nor_1_out, or_3_out, or_4_out, or_5_out, or_6_out;

  buf I14 (I14_out, NRD);
  buf I16 (I16_out, NDI_ULA);
  buf I13 (I13_out, NWR);
  buf buffer_1 (buffer_1_out, NIORQ);
  buf I3 (I3_out, A1);
  buf I2 (I2_out, A0);
  buf I3_2 (I3_2_out, DI_32765);
  buf I4 (I4_out, A5);
  buf I5 (I5_out, A7);
  buf I15 (I15_out, NM1);
  buf I1 (I1_out, A14);
  buf I2_2 (I2_2_out, A15);
  or or_1 (NIN254, I14_out, or_3_out);
  or or_2 (NOUT254, I13_out, or_3_out);
  or or_3 (or_3_out, I16_out, I2_out, buffer_1_out, ~I4_out, ~I5_out, ~I3_out);  // OR_Gate
  or or_4 (or_4_out, I3_out, I2_2_out, ~I2_out, ~I1_out);  // OR_Gate
  or or_5 (or_5_out, I3_2_out, buffer_1_out, I13_out);
  or or_6 (or_6_out, ~I4_out, ~I5_out);  // OR_Gate
  nor nor_1 (nor_1_out, ~I4_out, ~I5_out, I3_out, buffer_1_out);  // NOR_Gate
  nor nor_2 (CS_32765, or_4_out, or_5_out, or_6_out);
  nand nand_1 (nand_1_out, I15_out, I1_out);
  nand nand_2 (nand_2_out, nor_1_out, I2_2_out);
  nor nor_3 (BC1, nand_1_out, nand_2_out);
  nor nor_4 (BDIR, nand_2_out, I13_out);
endmodule
