// Logisim project video_512k.circ as structural Verilog: 1 circuit, main circuit main
module main (
  input  CLK,
  input  A,
  input  B,
  output Q0,
  output Q1,
  output Q2,
  output Q3,
  output Y
);

  wire and_1_out, and_2_out, and_3_out, and_4_out, and_5_out, and_6_out, and_7_out, and_8_out, and_9_out,
       and_10_out, clock_1_out, not_1_out, not_2_out, or_1_out, or_3_out, or_4_out, or_5_out, T1_qn, T2_qn,
       T3_2_qn, T3_qn;

  Clock clock_1 (.out(clock_1_out));
  or or_1 (or_1_out, CLK, clock_1_out);
  not not_1 (not_1_out, B);
  not not_2 (not_2_out, A);
  D_Flip_Flop T1 (.clk(or_1_out), .D(T1_qn), .Q(Q0), .Qn(T1_qn));  // open: preset, reset
  and and_1 (and_1_out, A, not_1_out);
  and and_2 (and_2_out, not_2_out, B);
  or or_2 (Y, and_1_out, and_2_out);
  and and_3 (and_3_out, Q1, T1_qn);
  and and_4 (and_4_out, Q0, T2_qn);
  or or_3 (or_3_out, and_3_out, and_4_out);
  D_Flip_Flop T2 (.clk(or_1_out), .D(or_3_out), .Q(Q1), .Qn(T2_qn));  // open: preset, reset
  and and_5 (and_5_out, Q1, Q0);
  and and_6 (and_6_out, Q2, ~and_5_out);  // AND_Gate
  and and_7 (and_7_out, T3_qn, and_5_out);
  or or_4 (or_4_out, and_6_out, and_7_out);
  D_Flip_Flop T3 (.clk(or_1_out), .D(or_4_out), .Q(Q2), .Qn(T3_qn));  // open: preset, reset
  and and_8 (and_8_out, Q2, and_5_out);
  and and_9 (and_9_out, Q3, ~and_8_out);  // AND_Gate
  and and_10 (and_10_out, T3_2_qn, and_8_out);
  or or_5 (or_5_out, and_9_out, and_10_out);
  D_Flip_Flop T3_2 (.clk(or_1_out), .D(or_5_out), .Q(Q3), .Qn(T3_2_qn));  // open: preset, reset
endmodule
